# Fritzing sketch big button midi (saved by Fritzing 0.9.3b)
stripboards: 1

parts:
  Arduino_Nano = Arduino Nano (Rev3.0)
  IC1 = IC, DIP package, 8 pins [chip_label=6N138]
  S1 = Round Pushbutton
  R2 = Resistor [tolerance=±5% resistance=220 package="1206 [SMD]"]
  R3 = Resistor [tolerance=±5% resistance=480 package="1206 [SMD]"]
  C1 = Ceramic Capacitor [capacitance=100nF package="100 mil [THT, multilayer]"]
  MIDI_IN = DIN-5 jack (MIDI) [package=THT]
  R4 = Resistor [tolerance=±5% resistance=4.7k package=THT]
  R5 = Resistor [tolerance=±5% resistance=220 package=THT]
  MIDI_THRU = DIN-5 jack (MIDI) [package=THT]
  D1_1N914 = Diode [package=diode-1n4148]
  R1 = Resistor [tolerance=±5% resistance=220 package="2010 [SMD]"]
  R6 = Resistor [tolerance=±5% resistance=10k package=THT]
  Q1_2N3904 = NPN-Transistor [package="TO92 [THT]"]
  R7 = Resistor [tolerance=±5% resistance=220 package=THT]

nets:
  N1: Arduino_Nano.D0/RX, IC1.pin6, R2.Pin_1, Q1_2N3904.B
  GND: Arduino_Nano.GND, IC1.pin5, R3.Pin_0, C1.0, R4.Pin_1, MIDI_THRU.2
  5V: Arduino_Nano.5V, IC1.pin8, R2.Pin_0, R5.Pin_0, R6.Pin_1, Q1_2N3904.C, R7.Pin_1
  N2: Arduino_Nano.A4, S1.leg0
  N3: IC1.pin2, D1_1N914.A, R1.Pin_1
  N4: IC1.pin3, MIDI_IN.5, D1_1N914.C
  N5: IC1.pin7, R4.Pin_0
  N6: S1.leg1, R6.Pin_0
  N7: R3.Pin_1, R5.Pin_1, MIDI_THRU.5, Q1_2N3904.E
  N8: C1.1, MIDI_IN.2
  N9: MIDI_IN.4, R1.Pin_0
  N10: MIDI_THRU.4, R7.Pin_0

notes:
  MIDI IN
  MIDI THRU
  +5V (pin 4)
  Signal (pin 5)
  Serial In (pin 1/RX)
  Alt/Shift Button
  Big Button/Hex Drum MIDI modification
